# Fritzing sketch arduino_humiditylogger (saved by Fritzing 0.9.0b)
breadboards: 1

parts:
  Part1 = Arduino Uno (Rev3)
  U1 = HIH-4030 [package=hih-4030]
  U2 = TEMPERATURE-SENSOR [package=to-92]
  Part2 = Arduino Ethernet Shield (Rev3)
  R1 = Resistor [tolerance=±2% resistance=4.7k package=THT]  # not connected

nets:
  N1: Part1.A0, U1.OUT
  5V: Part1.5V, U1.VCC
  GND: Part1.GND, U1.GND
  GND_2: U2.GND, Part2.GND
  N2: U2.ADJ, Part2.D2

notes:
  DS1820
  HIH-4030
